// Logisim project CMPC.circ as structural Verilog: 22 circuits, main circuit computer
module computer (
  input  reset,
  input  [6:0] keyboardChar,
  input  keyPress,
  output [31:0] LEDBUS0,
  output [31:0] LEDBUS1,
  output [31:0] LEDBUS2,
  output [31:0] LEDBUS3,
  output [31:0] LEDBUS4,
  output [31:0] LEDBUS5,
  output [31:0] LEDBUS6,
  output [31:0] LEDBUS7,
  output ttyClk,
  output ttyWriteSig,
  output [6:0] ttyCharout,
  output ConsumeKBF
);

  wire addressdecoder_1_iow1, addressdecoder_1_iow2, addressdecoder_1_iow3, addressdecoder_1_iow4,
       addressdecoder_1_iow5, addressdecoder_1_ramwrite, cpu_1_cpuclk, cpu_1_memaccessmode,
       cpu_1_memstoreflag, interrupt_1_cpuinterrupt, interrupt_1_keyboardenable, interrupt_1_matrixenable,
       interrupt_1_timerenable, interrupt_1_ttyenable, keyboardinterface_1_interruptsig, timer_1_interruptsig;
  wire [2:0] addressdecoder_1_readselect;
  wire [25:0] addressdecoder_1_decodedaddr;
  wire [31:0] byteram_1_output, cpu_1_memaddres, cpu_1_memwritedata, interrupt_1_out_7,
       keyboardinterface_1_output, ledmatrixinterface_1_outputreadbuffer, multiplexer_1_out, timer_1_output;

  CPU cpu_1 (
    .Reset(reset), .cpuCLK(cpu_1_cpuclk), .memWriteData(cpu_1_memwritedata), .memRead(multiplexer_1_out),
    .memAddres(cpu_1_memaddres), .memAccessMode(cpu_1_memaccessmode), .memStoreFlag(cpu_1_memstoreflag),
    .interrupt(interrupt_1_cpuinterrupt));
  AddressDecoder addressdecoder_1 (
    .Address(cpu_1_memaddres), .WriteFlag(cpu_1_memstoreflag), .decodedAddr(addressdecoder_1_decodedaddr),
    .IOW3(addressdecoder_1_iow3), .IOW2(addressdecoder_1_iow2), .IOW1(addressdecoder_1_iow1),
    .RAMwrite(addressdecoder_1_ramwrite), .readSelect(addressdecoder_1_readselect),
    .IOW4(addressdecoder_1_iow4), .IOW5(addressdecoder_1_iow5));
  byteRam byteram_1 (
    .mode_0_byte_1_word(cpu_1_memaccessmode), .D(cpu_1_memwritedata), .A(addressdecoder_1_decodedaddr),
    .store(addressdecoder_1_ramwrite), .Clock(cpu_1_cpuclk), .\output (byteram_1_output));
  Interrupt interrupt_1 (
    .CLK(cpu_1_cpuclk), .write(addressdecoder_1_iow1), .addr(addressdecoder_1_decodedaddr),
    .data(cpu_1_memwritedata), .out_7(interrupt_1_out_7), .timerInterrupt(timer_1_interruptsig),
    .keyboardInterrupt(keyboardinterface_1_interruptsig), .cpuInterrupt(interrupt_1_cpuinterrupt),
    .timerEnable(interrupt_1_timerenable), .keyboardEnable(interrupt_1_keyboardenable),
    .MatrixEnable(interrupt_1_matrixenable), .TTYenable(interrupt_1_ttyenable));
  Multiplexer #(.select(3), .width(32), .enable("false")) multiplexer_1 (
    .in0(byteram_1_output), .in1(interrupt_1_out_7), .in2(timer_1_output),
    .in3(ledmatrixinterface_1_outputreadbuffer), .in5(keyboardinterface_1_output), .out(multiplexer_1_out),
    .sel(addressdecoder_1_readselect));  // open: in4, in6, in7
  Timer timer_1 (
    .deviceEnable(interrupt_1_timerenable), .CLK(cpu_1_cpuclk), .write(addressdecoder_1_iow2),
    .Data(cpu_1_memwritedata), .\output (timer_1_output), .InterruptSig(timer_1_interruptsig));
  KeyboardInterface keyboardinterface_1 (
    .CLK(cpu_1_cpuclk), .keyboardChar(keyboardChar), .enableDevice(interrupt_1_keyboardenable),
    .write(addressdecoder_1_iow5), .keyPress(keyPress), .data(cpu_1_memwritedata),
    .ConsumeBuffer(ConsumeKBF), .\output (keyboardinterface_1_output),
    .interruptSig(keyboardinterface_1_interruptsig));
  TTYInterface ttyinterface_1 (
    .enableDevice(interrupt_1_ttyenable), .write(addressdecoder_1_iow4), .Data(cpu_1_memwritedata),
    .CLK(cpu_1_cpuclk), .writeSigOut(ttyWriteSig), .charOut(ttyCharout), .clkOut(ttyClk));
  LEDMatrixInterface ledmatrixinterface_1 (
    .Write(addressdecoder_1_iow3), .CLK(cpu_1_cpuclk), .Data(cpu_1_memwritedata),
    .Address(addressdecoder_1_decodedaddr), .LB0(LEDBUS0), .LB1(LEDBUS1), .LB2(LEDBUS2), .LB3(LEDBUS3),
    .LB4(LEDBUS4), .LB5(LEDBUS5), .LB6(LEDBUS6), .LB7(LEDBUS7),
    .outputReadbuffer(ledmatrixinterface_1_outputreadbuffer), .Enable(interrupt_1_matrixenable));
endmodule

module CPU (
  input  [31:0] memRead,
  input  interrupt,
  input  Reset,
  output cpuCLK,
  output [31:0] memWriteData,
  output [31:0] memAddres,
  output memAccessMode,
  output memStoreFlag
);

  wire alu_1_zero, and_1_out, bitselector_5_out, control_1_branch, control_1_branchcomparator,
       control_1_epcwrite, control_1_fetch, control_1_immflag, control_1_immzeroext, control_1_jump,
       control_1_link, control_1_memread, control_1_regwrite, control_1_specread,
       interruptionfsm_1_interruptstate, multiplexer_13_out, not_1_out, not_2_out, or_1_out, or_2_out,
       or_3_out, signaler_1_signal, xnor_1_out;
  wire [3:0] multiplexer_4_out, multiplexer_5_out, multiplexer_6_out, regdecoder_1_reg1, regdecoder_1_reg2,
       regdecoder_1_regdest;
  wire [4:0] control_1_aluop;
  wire [7:0] bitselector_3_out;
  wire [23:0] adder_1_out, adder_2_out, bitselector_1_out, bitselector_2_out, bitselector_4_out,
       multiplexer_1_out, multiplexer_2_out, multiplexer_3_out, multiplexer_9_out, PC_q, specregs_1_readdata;
  wire [31:0] alu_1_out, bit_extender_1_out, bit_extender_2_out, bit_extender_3_out,
       immextender_1_immextended, IR_q, multiplexer_7_out, multiplexer_10_out, multiplexer_11_out,
       multiplexer_14_out, registers_1_rsval, shifter_1_out;

  and and_1 (and_1_out, control_1_branch, xnor_1_out);
  Multiplexer #(.width(24), .enable("false")) multiplexer_1 (
    .in0(multiplexer_3_out), .in1(adder_2_out), .out(multiplexer_1_out), .sel(and_1_out));
  Multiplexer #(.width(24), .enable("false")) multiplexer_2 (
    .in0(specregs_1_readdata), .in1(multiplexer_1_out), .out(multiplexer_2_out), .sel(not_1_out));
  not not_1 (not_1_out, signaler_1_signal);
  Multiplexer #(.width(24), .enable("false")) multiplexer_3 (
    .in0(multiplexer_9_out), .in1(bitselector_1_out), .out(multiplexer_3_out), .sel(control_1_jump));
  Multiplexer #(.width(4), .enable("false")) multiplexer_4 (
    .in0(regdecoder_1_reg2), .in1(regdecoder_1_regdest), .out(multiplexer_4_out), .sel(or_1_out));
  Register #(.width(24)) PC (.D(multiplexer_2_out), .Q(PC_q), .clk(cpuCLK), .clr(Reset));  // open: en
  or or_1 (or_1_out, control_1_branch, or_3_out);
  xnor xnor_1 (xnor_1_out, control_1_branchcomparator, alu_1_zero);
  BitSelector #(.width(32), .group(24)) bitselector_1 (.in(registers_1_rsval), .out(bitselector_1_out), .sel(1'b0));
  Multiplexer #(.width(4), .enable("false")) multiplexer_5 (
    .in0(regdecoder_1_reg1), .in1(regdecoder_1_regdest), .out(multiplexer_5_out), .sel(control_1_jump));
  Multiplexer #(.width(4), .enable("false")) multiplexer_6 (
    .in0(regdecoder_1_regdest), .in1(regdecoder_1_reg1), .out(multiplexer_6_out), .sel(control_1_link));
  Clock CLK (.out(cpuCLK));
  Multiplexer #(.width(32), .enable("false")) multiplexer_7 (
    .in0(multiplexer_11_out), .in1(bit_extender_1_out), .out(multiplexer_7_out), .sel(control_1_link));
  regDecoder regdecoder_1 (
    .instruction(IR_q), .regDest(regdecoder_1_regdest), .reg2(regdecoder_1_reg2), .reg1(regdecoder_1_reg1));
  Registers registers_1 (
    .Source(multiplexer_5_out), .RSval(registers_1_rsval), .Clock(cpuCLK), .Data(multiplexer_7_out),
    .WriteFlag(control_1_regwrite), .Target(multiplexer_4_out), .RTval(memWriteData),
    .Destination(multiplexer_6_out));
  BitSelector #(.width(32), .group(24)) bitselector_2 (
    .in(immextender_1_immextended), .out(bitselector_2_out), .sel(1'b0));
  Adder #(.width(24)) adder_1 (.a(PC_q), .b(24'h1), .out(adder_1_out));  // open: cin, cout
  Adder #(.width(24)) adder_2 (.a(bitselector_2_out), .b(PC_q), .out(adder_2_out));  // open: cin, cout
  Multiplexer #(.width(32), .enable("false")) multiplexer_8 (
    .in1({32{1'b0}}), .sel(signaler_1_signal));  // open: in0, out
  Multiplexer #(.width(24), .enable("false")) multiplexer_9 (
    .in0(adder_1_out), .in1(PC_q), .out(multiplexer_9_out), .sel(control_1_fetch));
  Register #(.width(32)) IR (.D(memRead), .en(control_1_fetch), .Q(IR_q), .clk(cpuCLK), .clr(Reset));
  Multiplexer #(.width(32), .enable("false")) multiplexer_10 (
    .in0(memWriteData), .in1(immextender_1_immextended), .out(multiplexer_10_out), .sel(control_1_immflag));
  assign bit_extender_1_out = {{8{1'b0}}, adder_1_out};  // Bit_Extender bit_extender_1
  ImmExtender immextender_1 (.zero(control_1_immzeroext), .ImmExtended(immextender_1_immextended), .Instruction(IR_q));
  BitSelector #(.width(32), .group(8)) bitselector_3 (.in(IR_q), .out(bitselector_3_out), .sel(2'b11));
  ALU alu_1 (
    .op(control_1_aluop), .a(registers_1_rsval), .b(multiplexer_10_out), .out(alu_1_out), .zero(alu_1_zero));  // open: cbit
  Multiplexer #(.width(32), .enable("false")) multiplexer_11 (
    .in0(alu_1_out), .in1(multiplexer_14_out), .out(multiplexer_11_out), .sel(control_1_memread));
  or or_2 (or_2_out, Reset, signaler_1_signal);
  control control_1 (
    .opcode(bitselector_3_out), .ALUop(control_1_aluop), .jump(control_1_jump), .\byte (memAccessMode),
    .memread(control_1_memread), .memwrite(memStoreFlag), .regwrite(control_1_regwrite),
    .immflag(control_1_immflag), .branch(control_1_branch), .branchcomparator(control_1_branchcomparator),
    .fetch(control_1_fetch), .clk(cpuCLK), .link(control_1_link), .ClearFetch(or_2_out),
    .ImmZeroExt(control_1_immzeroext), .specRead(control_1_specread), .EPCwrite(control_1_epcwrite));
  assign bit_extender_2_out = {{8{1'b0}}, PC_q};  // Bit_Extender bit_extender_2
  Shifter #(.width(32)) shifter_1 (.in(bit_extender_2_out), .\dist (5'b00010), .out(shifter_1_out));
  or or_3 (or_3_out, control_1_epcwrite, memStoreFlag);
  BitSelector #(.width(32), .group(24)) bitselector_4 (.in(memWriteData), .out(bitselector_4_out), .sel(1'b0));
  Multiplexer #(.width(32), .enable("false")) multiplexer_12 (
    .in0(alu_1_out), .in1(shifter_1_out), .out(memAddres), .sel(control_1_fetch));
  not not_2 (not_2_out, interruptionfsm_1_interruptstate);
  BitSelector #(.width(32)) bitselector_5 (.in(memAddres), .out(bitselector_5_out), .sel({5{1'b0}}));
  Multiplexer #(.enable("false")) multiplexer_13 (
    .in0(bitselector_5_out), .in1(1'b1), .out(multiplexer_13_out), .sel(signaler_1_signal));
  Multiplexer #(.width(32), .enable("false")) multiplexer_14 (
    .in0(memRead), .in1(bit_extender_3_out), .out(multiplexer_14_out), .sel(control_1_specread));
  interruptionFSM interruptionfsm_1 (
    .CLK(cpuCLK), .fetch(control_1_fetch), .interrupt(interrupt),
    .interruptState(interruptionfsm_1_interruptstate));
  specRegs specregs_1 (
    .EPCdata(bitselector_4_out), .CLK(cpuCLK), .writeNPC(not_2_out), .writeEPC(control_1_epcwrite),
    .PPCdata(PC_q), .readAddr(multiplexer_13_out), .readData(specregs_1_readdata));
  signaler signaler_1 (.CLK(cpuCLK), .\input (interruptionfsm_1_interruptstate), .signal(signaler_1_signal));
  assign bit_extender_3_out = {{8{1'b0}}, specregs_1_readdata};  // Bit_Extender bit_extender_3
endmodule

// registers
module Registers (
  input  [3:0] Destination,
  input  WriteFlag,
  input  Clock,
  input  [31:0] Data,
  input  [3:0] Source,
  input  [3:0] Target,
  output [31:0] RSval,
  output [31:0] RTval
);

  wire and_1_out, and_2_out, and_3_out, and_4_out, and_5_out, and_6_out, and_7_out, and_8_out, and_9_out,
       and_10_out, and_11_out, and_12_out, and_13_out, and_14_out, and_15_out, and_16_out, decoder_1_out0,
       decoder_1_out1, decoder_1_out2, decoder_1_out3, decoder_1_out4, decoder_1_out5, decoder_1_out6,
       decoder_1_out7, decoder_1_out8, decoder_1_out9, decoder_1_out10, decoder_1_out11, decoder_1_out12,
       decoder_1_out13, decoder_1_out14, decoder_1_out15;
  wire [31:0] _0_q, a0_q, a1_q, a2_q, at_q, fp_q, gp_q, ra_q, s0_q, s1_q, s2_q, sp_q, t0_q, t1_q, v0_q, v1_q;

  Decoder #(.select(4), .enable("false")) decoder_1 (
    .out0(decoder_1_out0), .out1(decoder_1_out1), .out2(decoder_1_out2), .out3(decoder_1_out3),
    .out4(decoder_1_out4), .out5(decoder_1_out5), .out6(decoder_1_out6), .out7(decoder_1_out7),
    .out8(decoder_1_out8), .out9(decoder_1_out9), .out10(decoder_1_out10), .out11(decoder_1_out11),
    .out12(decoder_1_out12), .out13(decoder_1_out13), .out14(decoder_1_out14), .out15(decoder_1_out15),
    .sel(Destination));
  and and_1 (and_1_out, decoder_1_out8, WriteFlag);
  and and_2 (and_2_out, decoder_1_out9, WriteFlag);
  and and_3 (and_3_out, decoder_1_out10, WriteFlag);
  and and_4 (and_4_out, decoder_1_out12, WriteFlag);
  and and_5 (and_5_out, decoder_1_out0, 1'b0);
  and and_6 (and_6_out, decoder_1_out1, WriteFlag);
  and and_7 (and_7_out, decoder_1_out2, WriteFlag);
  and and_8 (and_8_out, decoder_1_out3, WriteFlag);
  and and_9 (and_9_out, decoder_1_out4, WriteFlag);
  and and_10 (and_10_out, decoder_1_out5, WriteFlag);
  and and_11 (and_11_out, decoder_1_out6, WriteFlag);
  and and_12 (and_12_out, decoder_1_out7, WriteFlag);
  and and_13 (and_13_out, decoder_1_out11, WriteFlag);
  and and_14 (and_14_out, decoder_1_out13, WriteFlag);
  and and_15 (and_15_out, decoder_1_out14, WriteFlag);
  and and_16 (and_16_out, decoder_1_out15, WriteFlag);
  Register #(.width(32)) _0 (.D(Data), .en(and_5_out), .Q(_0_q), .clk(Clock));  // open: clr
  Register #(.width(32)) v0 (.D(Data), .en(and_6_out), .Q(v0_q), .clk(Clock));  // open: clr
  Register #(.width(32)) v1 (.D(Data), .en(and_7_out), .Q(v1_q), .clk(Clock));  // open: clr
  Register #(.width(32)) a0 (.D(Data), .en(and_8_out), .Q(a0_q), .clk(Clock));  // open: clr
  Register #(.width(32)) a1 (.D(Data), .en(and_9_out), .Q(a1_q), .clk(Clock));  // open: clr
  Register #(.width(32)) a2 (.D(Data), .en(and_10_out), .Q(a2_q), .clk(Clock));  // open: clr
  Register #(.width(32)) t0 (.D(Data), .en(and_11_out), .Q(t0_q), .clk(Clock));  // open: clr
  Register #(.width(32)) t1 (.D(Data), .en(and_12_out), .Q(t1_q), .clk(Clock));  // open: clr
  Register #(.width(32)) at (.D(Data), .en(and_1_out), .Q(at_q), .clk(Clock));  // open: clr
  Register #(.width(32)) s0 (.D(Data), .en(and_2_out), .Q(s0_q), .clk(Clock));  // open: clr
  Register #(.width(32)) s1 (.D(Data), .en(and_3_out), .Q(s1_q), .clk(Clock));  // open: clr
  Register #(.width(32)) s2 (.D(Data), .en(and_13_out), .Q(s2_q), .clk(Clock));  // open: clr
  Register #(.width(32)) gp (.D(Data), .en(and_4_out), .Q(gp_q), .clk(Clock));  // open: clr
  Register #(.width(32)) sp (.D(Data), .en(and_14_out), .Q(sp_q), .clk(Clock));  // open: clr
  Register #(.width(32)) fp (.D(Data), .en(and_15_out), .Q(fp_q), .clk(Clock));  // open: clr
  Register #(.width(32)) ra (.D(Data), .en(and_16_out), .Q(ra_q), .clk(Clock));  // open: clr
  Multiplexer #(.select(4), .width(32), .enable("false")) multiplexer_1 (
    .in0(_0_q), .in1(v0_q), .in2(v1_q), .in3(a0_q), .in4(a1_q), .in5(a2_q), .in6(t0_q), .in7(t1_q),
    .in8(at_q), .in9(s0_q), .in10(s1_q), .in11(s2_q), .in12(gp_q), .in13(sp_q), .in14(fp_q), .in15(ra_q),
    .out(RTval), .sel(Target));
  Multiplexer #(.select(4), .width(32), .enable("false")) multiplexer_2 (
    .in0(_0_q), .in1(v0_q), .in2(v1_q), .in3(a0_q), .in4(a1_q), .in5(a2_q), .in6(t0_q), .in7(t1_q),
    .in8(at_q), .in9(s0_q), .in10(s1_q), .in11(s2_q), .in12(gp_q), .in13(sp_q), .in14(fp_q), .in15(ra_q),
    .out(RSval), .sel(Source));
endmodule

module ALU (
  input  [4:0] op,
  input  [31:0] a,
  input  [31:0] b,
  output [31:0] out,
  output cbit,
  output zero
);

  wire and_1_out, and_2_out, bitselector_4_out, not_2_out;
  wire [1:0] alumuxdec_1_y0;
  wire [4:0] bitselector_1_out, multiplexer_2_out;
  wire [15:0] bitselector_2_out, bitselector_3_out, divider_1_out, divider_1_rem, multiplier_1_cout,
       multiplier_1_out;
  wire [31:0] adder_1_out, and_3_out, bit_extender_1_out, multiplexer_1_out, multiplexer_3_out,
       multiplexer_4_out, not_1_out, not_3_out, or_1_out, shifter_1_out, shifter_2_out, shifter_3_out,
       xor_1_out;

  and and_1 (and_1_out, op[1], op[0]);
  assign not_1_out = ~b;  // NOT_Gate not_1, 32 bits wide
  BitSelector #(.width(32), .group(5)) bitselector_1 (.in(b), .out(bitselector_1_out), .sel(3'b000));
  not not_2 (not_2_out, op[1]);
  and and_2 (and_2_out, op[0], not_2_out);
  Multiplexer #(.width(32), .enable("false")) multiplexer_1 (
    .in0(b), .in1(not_1_out), .out(multiplexer_1_out), .sel(and_2_out));
  Multiplexer #(.width(5), .enable("false")) multiplexer_2 (
    .in0(bitselector_1_out), .in1(5'b10000), .out(multiplexer_2_out), .sel(and_1_out));
  BitSelector #(.width(32), .group(16)) bitselector_2 (.in(a), .out(bitselector_2_out), .sel(1'b0));
  BitSelector #(.width(32), .group(16)) bitselector_3 (.in(b), .out(bitselector_3_out), .sel(1'b0));
  Multiplexer #(.width(32), .enable("false")) multiplexer_3 (
    .in0(a), .in1(b), .out(multiplexer_3_out), .sel(and_1_out));
  ALUmuxDec alumuxdec_1 (
    .B0(op[0]), .B1(op[1]), .B2(op[2]), .B4(op[4]), .Y0(alumuxdec_1_y0[0]), .Y1(alumuxdec_1_y0[1]));
  assign or_1_out = a | multiplexer_1_out;  // OR_Gate or_1, 32 bits wide
  assign and_3_out = a & multiplexer_1_out;  // AND_Gate and_3, 32 bits wide
  assign xor_1_out = a ^ multiplexer_1_out;  // XOR_Gate xor_1, 32 bits wide
  Adder #(.width(32)) adder_1 (.a(a), .b(multiplexer_1_out), .out(adder_1_out), .cin(and_2_out), .cout(cbit));
  Shifter #(.width(32)) shifter_1 (.in(multiplexer_3_out), .\dist (multiplexer_2_out), .out(shifter_1_out));
  Shifter #(.width(32), .shift("lr")) shifter_2 (
    .in(multiplexer_3_out), .\dist (multiplexer_2_out), .out(shifter_2_out));
  Shifter #(.width(32), .shift("ar")) shifter_3 (
    .in(multiplexer_3_out), .\dist (multiplexer_2_out), .out(shifter_3_out));
  BitSelector #(.width(32)) bitselector_4 (.in(adder_1_out), .out(bitselector_4_out), .sel({5{1'b1}}));
  assign bit_extender_1_out = {{31{1'b0}}, bitselector_4_out};  // Bit_Extender bit_extender_1
  Multiplier #(.width(16)) multiplier_1 (
    .a(bitselector_2_out), .b(bitselector_3_out), .out(multiplier_1_out), .cout(multiplier_1_cout));  // open: cin
  Divider #(.width(16)) divider_1 (
    .a(bitselector_2_out), .b(bitselector_3_out), .out(divider_1_out), .rem(divider_1_rem));  // open: upper
  Multiplexer #(.select(3), .width(32), .enable("false")) multiplexer_4 (
    .in0(or_1_out), .in1(and_3_out), .in2(xor_1_out), .in3(adder_1_out), .in4(shifter_1_out),
    .in5(shifter_2_out), .in6(shifter_3_out), .in7(bit_extender_1_out), .out(multiplexer_4_out), .sel(op[4:2]));
  assign not_3_out = ~multiplexer_4_out;  // NOT_Gate not_3, 32 bits wide
  zerocheck zerocheck_1 (.\input (adder_1_out), .zeroflag(zero));
  Multiplexer #(.select(2), .width(32), .enable("false")) multiplexer_5 (
    .in0(multiplexer_4_out), .in1(not_3_out), .in2({multiplier_1_cout, multiplier_1_out}),
    .in3({divider_1_rem, divider_1_out}), .out(out), .sel(alumuxdec_1_y0));

  // Notes on the sheet:
  //   ALU mux decoder
endmodule

module zerocheck (
  input  [31:0] \input ,
  output zeroflag
);

  nor nor_1 (zeroflag, \input [0], \input [1], \input [2], \input [3], \input [4], \input [5], \input [6], \input [7], \input [8], \input [9], \input [10], \input [11], \input [12], \input [13], \input [14], \input [15], \input [16], \input [17], \input [18], \input [19], \input [20], \input [21], \input [22], \input [23], \input [24], \input [25], \input [26], \input [27], \input [28], \input [29], \input [30], \input [31]);
endmodule

module control (
  input  [7:0] opcode,
  input  clk,
  input  ClearFetch,
  output [4:0] ALUop,
  output jump,
  output ImmZeroExt,
  output link,
  output \byte ,
  output memread,
  output memwrite,
  output regwrite,
  output immflag,
  output branch,
  output branchcomparator,
  output fetch,
  output specRead,
  output EPCwrite
);

  wire not_1_out, not_2_out, not_3_out, not_4_out, subcontroller_1_branch, subcontroller_1_byte,
       subcontroller_1_epcwrite, subcontroller_1_jump, subcontroller_1_link, subcontroller_1_memwrite,
       subcontroller_1_regwrite;
  wire [1:0] bitselector_1_out;

  ALUtranslator alutranslator_1 (
    .a(opcode[3]), .b(opcode[2]), .c(opcode[1]), .d(opcode[0]), .A_2(ALUop[4]), .B_2(ALUop[3]),
    .C_2(ALUop[2]), .D_2(ALUop[1]), .E(ALUop[0]));
  D_Flip_Flop d_ff_1 (.clk(clk), .D(fetch), .Qn(fetch), .reset(ClearFetch));  // open: Q, preset, en
  subcontroller subcontroller_1 (
    .a(opcode[7]), .jump(subcontroller_1_jump), .b(opcode[6]), .link(subcontroller_1_link), .c(opcode[5]),
    .\byte (subcontroller_1_byte), .d(opcode[4]), .memread(memread), .memwrite(subcontroller_1_memwrite),
    .regWrite(subcontroller_1_regwrite), .immflag(immflag), .branch(subcontroller_1_branch),
    .branchcomparator(branchcomparator), .specRead(specRead), .EPCwrite(subcontroller_1_epcwrite));
  not not_1 (not_1_out, fetch);
  and and_1 (EPCwrite, not_1_out, subcontroller_1_epcwrite);
  not not_2 (not_2_out, fetch);
  or or_1 (\byte , subcontroller_1_byte, fetch);
  not not_3 (not_3_out, fetch);
  and and_2 (jump, subcontroller_1_jump, not_2_out);
  and and_3 (regwrite, subcontroller_1_regwrite, not_3_out);
  and and_4 (link, not_2_out, subcontroller_1_link);
  and and_5 (branch, not_3_out, subcontroller_1_branch);
  and and_6 (memwrite, subcontroller_1_memwrite, not_3_out);
  BitSelector #(.width(5), .group(2)) bitselector_1 (.in(ALUop), .out(bitselector_1_out), .sel(2'b01));
  Multiplexer #(.select(2), .enable("false")) multiplexer_1 (
    .in0(1'b1), .in1(1'b1), .in2(1'b1), .in3(not_4_out), .out(ImmZeroExt), .sel(bitselector_1_out));
  not not_4 (not_4_out, 1'b1);
endmodule

module ALUtranslator (
  input  a,
  input  b,
  input  c,
  input  d,
  output A_2,
  output B_2,
  output C_2,
  output D_2,
  output E
);

  wire and_1_out, and_2_out, and_3_out, and_4_out, and_5_out, and_6_out, and_7_out, and_8_out, and_9_out,
       and_10_out, and_11_out, and_12_out, and_13_out, and_14_out, and_15_out, and_16_out, and_17_out,
       and_18_out, and_19_out, not_1_out, not_2_out, not_3_out, not_4_out, not_5_out, not_6_out, not_7_out,
       not_8_out, not_9_out, not_10_out, not_11_out, not_12_out, not_13_out, not_14_out, not_15_out,
       not_16_out, not_17_out, not_18_out, not_19_out, not_20_out, not_21_out, not_22_out, not_23_out,
       not_24_out;

  and and_1 (and_1_out, b, c, d);
  not not_1 (not_1_out, b);
  and and_2 (and_2_out, a, not_1_out, not_2_out);
  not not_2 (not_2_out, c);
  and and_3 (and_3_out, a, not_3_out, not_4_out);
  not not_3 (not_3_out, b);
  not not_4 (not_4_out, d);
  not not_5 (not_5_out, c);
  and and_4 (and_4_out, a, not_5_out, not_6_out);
  not not_6 (not_6_out, d);
  not not_7 (not_7_out, a);
  not not_8 (not_8_out, d);
  not not_9 (not_9_out, b);
  not not_10 (not_10_out, d);
  not not_11 (not_11_out, a);
  not not_12 (not_12_out, c);
  not not_13 (not_13_out, b);
  not not_14 (not_14_out, a);
  and and_5 (and_5_out, not_14_out, not_15_out, d);
  not not_15 (not_15_out, c);
  not not_16 (not_16_out, a);
  and and_6 (and_6_out, not_16_out, b, not_17_out);
  not not_17 (not_17_out, d);
  not not_18 (not_18_out, b);
  and and_7 (and_7_out, a, not_18_out, not_19_out);
  not not_19 (not_19_out, d);
  and and_8 (and_8_out, a, b, c);
  not not_20 (not_20_out, b);
  and and_9 (and_9_out, not_20_out, c, d);
  and and_10 (and_10_out, b, not_21_out, not_22_out);
  not not_21 (not_21_out, c);
  not not_22 (not_22_out, d);
  and and_11 (and_11_out, a, b);
  and and_12 (and_12_out, b, c, not_23_out);
  not not_23 (not_23_out, d);
  and and_13 (and_13_out, a, c, not_24_out);
  not not_24 (not_24_out, d);
  and and_14 (and_14_out, a, b);
  or or_1 (A_2, and_1_out, and_2_out, and_3_out, and_4_out);
  and and_15 (and_15_out, not_7_out, c, not_8_out);
  and and_16 (and_16_out, not_9_out, c, not_10_out);
  and and_17 (and_17_out, not_11_out, b, not_12_out, d);
  and and_18 (and_18_out, a, not_13_out, d);
  and and_19 (and_19_out, a, c, d);
  or or_2 (C_2, and_5_out, and_6_out, and_7_out, and_8_out);
  or or_3 (D_2, and_9_out, and_10_out, and_11_out);
  or or_4 (E, and_12_out, and_13_out, and_14_out);
  or or_5 (B_2, and_15_out, and_16_out, and_17_out, and_18_out, and_19_out);
endmodule

module byteRam (
  input  mode_0_byte_1_word,
  input  [31:0] D,
  input  [25:0] A,
  input  store,
  input  Clock,
  output [31:0] \output 
);

  wire [1:0] bitselector_1_out;
  wire [4:0] bit_extender_1_out, shifter_2_out;
  wire [7:0] bitselector_2_out, multiplexer_2_out;
  wire [23:0] bitselector_3_out;
  wire [25:0] shifter_1_out;
  wire [31:0] bit_extender_2_out, bit_extender_3_out, multiplexer_1_out, or_1_out, ram_1_data, shifter_3_out;

  BitSelector #(.width(26), .group(2)) bitselector_1 (.in(A), .out(bitselector_1_out), .sel(4'b0000));
  BitSelector #(.width(32), .group(8)) bitselector_2 (.in(D), .out(bitselector_2_out), .sel(2'b00));
  Shifter #(.width(26), .shift("lr")) shifter_1 (.in(A), .\dist (5'b00010), .out(shifter_1_out));
  assign bit_extender_1_out = {{3{1'b0}}, bitselector_1_out};  // Bit_Extender bit_extender_1
  BitSelector #(.width(26), .group(24)) bitselector_3 (.in(shifter_1_out), .out(bitselector_3_out), .sel(1'b0));
  Multiplexer #(.width(32), .enable("false")) multiplexer_1 (
    .in0(or_1_out), .in1(D), .out(multiplexer_1_out), .sel(mode_0_byte_1_word));
  assign bit_extender_2_out = {{24{1'b0}}, bitselector_2_out};  // Bit_Extender bit_extender_2
  Shifter #(.width(5)) shifter_2 (.in(bit_extender_1_out), .\dist (3'b011), .out(shifter_2_out));
  Shifter #(.width(32)) shifter_3 (.in(bit_extender_2_out), .\dist (shifter_2_out), .out(shifter_3_out));
  RAM #(.addrWidth(24), .dataWidth(32), .bus("separate")) ram_1 (
    .addr(bitselector_3_out), .din(multiplexer_1_out), .data(ram_1_data), .str(store), .clk(Clock), .ld(1'b1));  // open: sel, clr
  assign or_1_out = shifter_3_out | ram_1_data;  // OR_Gate or_1, 32 bits wide
  Multiplexer #(.select(2), .width(8), .enable("false")) multiplexer_2 (
    .in0(ram_1_data[7:0]), .in1(ram_1_data[15:8]), .in2(ram_1_data[23:16]), .in3(ram_1_data[31:24]),
    .out(multiplexer_2_out), .sel(bitselector_1_out));
  assign bit_extender_3_out = {{24{1'b0}}, multiplexer_2_out};  // Bit_Extender bit_extender_3
  Multiplexer #(.width(32), .enable("false")) multiplexer_3 (
    .in0(bit_extender_3_out), .in1(ram_1_data), .out(\output ), .sel(mode_0_byte_1_word));
endmodule

module subcontroller (
  input  a,
  input  b,
  input  c,
  input  d,
  output jump,
  output link,
  output \byte ,
  output memread,
  output memwrite,
  output regWrite,
  output immflag,
  output branch,
  output branchcomparator,
  output specRead,
  output EPCwrite
);

  wire and_3_out, and_4_out, and_5_out, and_6_out, and_7_out, and_8_out, and_9_out, and_10_out, and_11_out,
       and_12_out, and_13_out, and_14_out, and_15_out, and_16_out, and_17_out, and_20_out, and_21_out,
       and_22_out, not_1_out, not_2_out, not_3_out, not_4_out, not_5_out, not_6_out, not_7_out, not_8_out,
       not_9_out, not_10_out, not_11_out, not_12_out, not_13_out, not_14_out, not_15_out, not_16_out,
       not_17_out, not_18_out, not_19_out, not_20_out, not_21_out;

  and and_1 (jump, b, c);
  and and_2 (link, b, c, d);
  not not_1 (not_1_out, c);
  or or_1 (\byte , not_1_out, b, a);
  not not_2 (not_2_out, b);
  and and_3 (and_3_out, not_2_out, c);
  and and_4 (and_4_out, b, not_3_out);
  not not_3 (not_3_out, c);
  and and_5 (and_5_out, a, d);
  and and_6 (and_6_out, a, b);
  not not_4 (not_4_out, a);
  not not_5 (not_5_out, b);
  not not_6 (not_6_out, c);
  not not_7 (not_7_out, a);
  not not_8 (not_8_out, b);
  and and_7 (and_7_out, not_7_out, not_8_out, not_9_out);
  not not_9 (not_9_out, c);
  not not_10 (not_10_out, a);
  and and_8 (and_8_out, not_10_out, not_11_out, not_12_out);
  not not_11 (not_11_out, c);
  not not_12 (not_12_out, d);
  not not_13 (not_13_out, b);
  and and_9 (and_9_out, not_13_out, c, not_14_out);
  not not_14 (not_14_out, d);
  and and_10 (and_10_out, b, c, d);
  and and_11 (and_11_out, a, b);
  not not_15 (not_15_out, a);
  and and_12 (and_12_out, not_15_out, not_16_out, d);
  not not_16 (not_16_out, b);
  not not_17 (not_17_out, b);
  and and_13 (and_13_out, not_17_out, c);
  and and_14 (and_14_out, b, not_18_out);
  not not_18 (not_18_out, c);
  and and_15 (and_15_out, a, b);
  and and_16 (and_16_out, a, not_19_out);
  not not_19 (not_19_out, c);
  and and_17 (and_17_out, a, b);
  not not_20 (not_20_out, d);
  or or_2 (branchcomparator, not_20_out, b);
  and and_18 (specRead, a, c, not_21_out);
  not not_21 (not_21_out, d);
  and and_19 (EPCwrite, a, c, d);
  or or_3 (memread, and_3_out, and_4_out, and_5_out, and_6_out);
  and and_20 (and_20_out, not_4_out, not_5_out, c, d);
  or or_4 (memwrite, and_20_out, and_21_out, and_22_out);
  and and_21 (and_21_out, b, not_6_out, d);
  and and_22 (and_22_out, a, b);
  or or_5 (regWrite, and_7_out, and_8_out, and_9_out, and_10_out, and_11_out);
  or or_6 (immflag, and_12_out, and_13_out, and_14_out, and_15_out);
  or or_7 (branch, and_16_out, and_17_out);
endmodule

module regDecoder (
  input  [31:0] instruction,
  output [3:0] regDest,
  output [3:0] reg2,
  output [3:0] reg1
);


  assign reg1 = instruction[19:16];
  assign reg2 = instruction[15:12];
  assign regDest = instruction[23:20];
endmodule

module ALUmuxDec (
  input  B0,
  input  B1,
  input  B2,
  input  B4,
  output Y0,
  output Y1
);

  wire and_1_out, and_2_out, not_1_out, not_2_out;

  not not_1 (not_1_out, B0);
  and and_1 (and_1_out, not_1_out, B1);
  and and_2 (and_2_out, B1, B2);
  and and_3 (Y1, B0, B1, not_2_out);
  not not_2 (not_2_out, B4);
  or or_1 (Y0, and_1_out, and_2_out);
endmodule

module AddressDecoder (
  input  [31:0] Address,
  input  WriteFlag,
  output [25:0] decodedAddr,
  output [2:0] readSelect,
  output IOW5,
  output IOW4,
  output IOW3,
  output IOW2,
  output IOW1,
  output RAMwrite
);

  BitSelector #(.width(6), .group(3)) bitselector_1 (.in(Address[31:26]), .out(readSelect), .sel(1'b0));
  Demultiplexer #(.select(3), .enable("false")) demultiplexer_1 (
    .out0(RAMwrite), .out1(IOW1), .out2(IOW2), .out3(IOW3), .out4(IOW4), .out5(IOW5), .in(WriteFlag),
    .sel(readSelect));  // open: out6, out7

  assign decodedAddr = Address[25:0];

  // Notes on the sheet:
  //   DeviceSelect 0: access RAM
  //   DeviceSelect = 6MSb(Address)
  //   Device Select X > 0: Access devic X
  //   26 LSb of Address input is address to access on device. 6 MSb of Adress input is the device address(Which device to read/write to)
endmodule

module ImmExtender (
  input  [31:0] Instruction,
  input  zero,
  output [31:0] ImmExtended
);

  wire [15:0] bitselector_1_out;
  wire [31:0] bit_extender_1_out, bit_extender_2_out;

  BitSelector #(.width(32), .group(16)) bitselector_1 (.in(Instruction), .out(bitselector_1_out), .sel(1'b0));
  assign bit_extender_1_out = {{16{bitselector_1_out[15]}}, bitselector_1_out};  // Bit_Extender bit_extender_1
  assign bit_extender_2_out = {{16{1'b0}}, bitselector_1_out};  // Bit_Extender bit_extender_2
  Multiplexer #(.width(32), .enable("false")) multiplexer_1 (
    .in0(bit_extender_1_out), .in1(bit_extender_2_out), .out(ImmExtended), .sel(zero));
endmodule

// intterrupt
module Interrupt (
  input  CLK,
  input  write,
  input  [25:0] addr,
  input  [31:0] data,
  input  timerInterrupt,
  input  keyboardInterrupt,
  output [31:0] out_7,
  output timerEnable,
  output keyboardEnable,
  output MatrixEnable,
  output TTYenable,
  output cpuInterrupt
);

  wire and_1_out, and_2_out, and_3_out, and_4_out, and_5_out, decoder_1_out0, decoder_1_out1, decoder_1_out2,
       not_1_out;
  wire [1:0] bitselector_1_out;
  wire [19:18] status_q_2;
  wire [31:0] keyboardConfig_q, MatrixConfig_q, multiplexer_1_out, timerConfig_q;
  wire [31:4] status_q;

  BitSelector #(.width(26), .group(2)) bitselector_1 (.in(addr), .out(bitselector_1_out), .sel(4'b0000));
  Decoder #(.select(2), .enable("false")) decoder_1 (
    .out0(decoder_1_out0), .out1(decoder_1_out1), .out2(decoder_1_out2), .sel(bitselector_1_out));  // open: out3
  // OR_Gate or_1 has open pins: in0=timerInterrupt, in1=keyboardInterrupt, out=open
  and and_1 (and_1_out, write, decoder_1_out0);
  and and_2 (and_2_out, write, decoder_1_out1);
  and and_3 (and_3_out, write, decoder_1_out2);
  not not_1 (not_1_out, write);
  Register #(.width(32)) timerConfig (.D(data), .en(and_1_out), .Q(timerConfig_q), .clk(CLK));  // open: clr
  Register #(.width(32)) keyboardConfig (.D(data), .en(and_2_out), .Q(keyboardConfig_q), .clk(CLK));  // open: clr
  Register #(.width(32)) MatrixConfig (.D(data), .en(and_3_out), .Q(MatrixConfig_q), .clk(CLK));  // open: clr
  Multiplexer #(.width(32), .enable("false")) multiplexer_1 (
    .in0(data),
    .in1({status_q[31:20], keyboardInterrupt, timerInterrupt, status_q[17:4], TTYenable, MatrixEnable, keyboardEnable, timerEnable}),
    .out(multiplexer_1_out), .sel(not_1_out));
  Register #(.width(32)) status (
    .D(multiplexer_1_out), .en(1'b1),
    .Q({status_q[31:20], status_q_2, status_q[17:4], TTYenable, MatrixEnable, keyboardEnable, timerEnable}),
    .clk(CLK));  // open: clr
  Multiplexer #(.select(2), .width(32), .enable("false")) multiplexer_2 (
    .in0(timerConfig_q), .in1(keyboardConfig_q), .in2(MatrixConfig_q),
    .in3({status_q[31:20], status_q_2, status_q[17:4], TTYenable, MatrixEnable, keyboardEnable, timerEnable}),
    .out(out_7), .sel(bitselector_1_out));
  and and_4 (and_4_out, status_q_2[18], timerEnable);
  or or_2 (cpuInterrupt, and_4_out, and_5_out);
  and and_5 (and_5_out, status_q_2[19], keyboardEnable);

  // Notes on the sheet:
  //   This is the interrupt device. It handles incoming interrupt signals from other devices. 
  //   There is one REE (Rising Edge to Edge) cycle delay before interrupt is forwarded to cpu if the incoming device is enabled for causing interrupts.
  //   In total it can take 4-5 REE before ISR routine is loaded into instruction register
endmodule

module specRegs (
  input  writeEPC,
  input  writeNPC,
  input  CLK,
  input  [23:0] PPCdata,
  input  [23:0] EPCdata,
  input  readAddr,
  output [23:0] readData
);

  wire [23:0] EPC_q, PPC_q;

  Register #(.width(24)) PPC (.D(PPCdata), .en(writeNPC), .Q(PPC_q), .clk(CLK));  // open: clr
  Register #(.width(24)) EPC (.D(EPCdata), .en(writeEPC), .Q(EPC_q), .clk(CLK));  // open: clr
  Multiplexer #(.width(24), .enable("false")) multiplexer_1 (.in0(PPC_q), .in1(EPC_q), .out(readData), .sel(readAddr));
endmodule

module signaler (
  input  CLK,
  input  \input ,
  output signal
);

  wire not_1_out;
  wire [1:0] d_ff_2_q, multiplexer_1_out, multiplexer_2_out;

  D_Flip_Flop d_ff_1 (.clk(CLK), .D(multiplexer_1_out[1]), .Q(d_ff_2_q[1]));  // open: Qn, preset, en, reset
  D_Flip_Flop d_ff_2 (.clk(CLK), .D(multiplexer_1_out[0]), .Q(d_ff_2_q[0]));  // open: Qn, preset, en, reset
  Multiplexer #(.width(2), .enable("false")) multiplexer_1 (
    .in0(2'b00), .in1(multiplexer_2_out), .out(multiplexer_1_out), .sel(\input ));
  Multiplexer #(.select(2), .width(2), .disabled(0), .enable("false")) multiplexer_2 (
    .in0(2'b01), .in1(2'b10), .in2(2'b10), .out(multiplexer_2_out), .sel(d_ff_2_q));  // open: in3
  and and_1 (signal, d_ff_2_q[0], not_1_out);
  not not_1 (not_1_out, d_ff_2_q[1]);
endmodule

module interruptionFSM (
  input  CLK,
  input  fetch,
  input  interrupt,
  output interruptState
);

  wire multiplexer_1_out, multiplexer_2_out, multiplexer_3_out, not_1_out, not_2_out, not_3_out;

  not not_1 (not_1_out, 1'b0);
  not not_2 (not_2_out, 1'b0);
  Multiplexer #(.select(2), .enable("false")) multiplexer_1 (
    .in0(1'b0), .in1(not_1_out), .in2(1'b0), .in3(not_2_out), .out(multiplexer_1_out),
    .sel({fetch, interrupt}));
  not not_3 (not_3_out, 1'b0);
  // Probe on multiplexer_1_out
  D_Flip_Flop d_ff_1 (.clk(CLK), .D(multiplexer_2_out), .Q(interruptState));  // open: Qn, preset, en, reset
  Multiplexer #(.enable("false")) multiplexer_2 (
    .in0(multiplexer_3_out), .in1(multiplexer_1_out), .out(multiplexer_2_out), .sel(interruptState));
  Multiplexer #(.select(2), .enable("false")) multiplexer_3 (
    .in0(1'b0), .in1(1'b0), .in2(1'b0), .in3(not_3_out), .out(multiplexer_3_out), .sel({fetch, interrupt}));
endmodule

module Timer (
  input  deviceEnable,
  input  CLK,
  input  write,
  input  [31:0] Data,
  output [31:0] \output ,
  output InterruptSig
);

  wire and_1_out, and_2_out, comparator_1_eq, not_2_out, not_3_out, not_4_out, or_1_out, or_2_out;
  wire [27:0] bitselector_1_out, counter_q;
  wire [31:0] multiplexer_1_out;
  wire [31:31] not_1_out;

  or or_1 (or_1_out, deviceEnable, write);
  and and_1 (and_1_out, or_1_out, CLK);
  not not_1 (not_1_out[31], not_4_out);
  not not_2 (not_2_out, not_4_out);
  or or_2 (or_2_out, write, not_2_out);
  not not_3 (not_3_out, and_1_out);
  Multiplexer #(.width(32), .enable("false")) multiplexer_1 (
    .in0({not_1_out[31], \output [30:0]}), .in1(Data), .out(multiplexer_1_out), .sel(write));
  and and_2 (and_2_out, not_3_out, not_4_out);
  Register #(.width(32)) confReg (.D(multiplexer_1_out), .en(or_2_out), .Q(\output ), .clk(and_1_out));  // open: clr
  Counter #(.width(28), .max('hfffffff)) counter (
    .Q(counter_q), .clk(and_2_out), .clr(write));  // open: load, D, count, carry
  BitSelector #(.width(32), .group(28)) bitselector_1 (.in(\output ), .out(bitselector_1_out), .sel(1'b0));
  Comparator #(.width(28)) comparator_1 (.a(bitselector_1_out), .b(counter_q), .eq(comparator_1_eq));  // open: gt, lt
  not not_4 (not_4_out, comparator_1_eq);
  BitSelector #(.width(32)) bitselector_2 (.in(\output ), .out(InterruptSig), .sel({5{1'b1}}));

  // Notes on the sheet:
  //   Outputs: output(read Data), InterruptSig(interrupt signal).
  //   Note: to be able to write to confReg you need to enable confREg from Interrupt subsystem
  //   Functionality description: A timer. Confreg holds number on which count reg equals causes an interrupt signal
  //   While in interrupt state  counter is not incremented. When writing to confReg counter is reset automatically.
  //   Note: Logisim tick frequency is innacurate and period between ticks can vary, especially for higher frequencies
  //   Inputs: Data(to write), Write(write enabled signal), CLK(clock signal), deviceEnable(When set device is enabled) 
  //   for Example picking 256Hz you might actually be getting 240Hz. Use show tick rate window option to see frequency live.
  //   it is possible to read/write to confreg. When counter == confReg trigger the MSb of confReg is set to 1 which then triggers interrupt sig
  //   Tc(Trigger count) : 28 LSb of confReg
  //   If(Interrupt flag): MSb of Cf
  //   Cf(Configuration flags): 4 MSb of confReg
  //   Timer delay = Tc/(Tick-frequency/2)
endmodule

module main (
);

  wire computer_1_consumekbf, computer_1_ttyclk, computer_1_ttywritesig, keyboard_1_avail, not_1_out,
       Reset_out;
  wire [6:0] computer_1_ttycharout, keyboard_1_data;
  wire [15:0] computer_1_ledbus2, computer_1_ledbus3, computer_1_ledbus3_2, computer_1_ledbus4,
       computer_1_ledbus4_2, computer_1_ledbus5, computer_1_ledbus6;
  wire [31:0] computer_1_ledbus0, computer_1_ledbus1, computer_1_ledbus7;
  wire [31:16] computer_1_ledbus2_2, computer_1_ledbus5_2, computer_1_ledbus6_2;

  Keyboard #(.buflen(1)) keyboard_1 (
    .clk(computer_1_consumekbf), .avail(keyboard_1_avail), .data(keyboard_1_data));  // open: re, clr
  Button Reset (.out(Reset_out));
  not not_1 (not_1_out, keyboard_1_avail);
  LED AccetingInput (.in(not_1_out));
  computer computer_1 (
    .reset(Reset_out), .LEDBUS0(computer_1_ledbus0), .LEDBUS1(computer_1_ledbus1),
    .LEDBUS2({computer_1_ledbus2_2, computer_1_ledbus2}),
    .LEDBUS3({computer_1_ledbus3_2, computer_1_ledbus3}),
    .LEDBUS4({computer_1_ledbus4_2, computer_1_ledbus4}),
    .LEDBUS5({computer_1_ledbus5_2, computer_1_ledbus5}),
    .LEDBUS6({computer_1_ledbus6_2, computer_1_ledbus6}), .LEDBUS7(computer_1_ledbus7),
    .ttyWriteSig(computer_1_ttywritesig), .ttyCharout(computer_1_ttycharout), .ttyClk(computer_1_ttyclk),
    .ConsumeKBF(computer_1_consumekbf), .keyboardChar(keyboard_1_data), .keyPress(keyboard_1_avail));
  DotMatrix #(.matrixcols(16), .matrixrows(16)) dotmatrix_1 (
    .col0(computer_1_ledbus0[15:0]), .col1(computer_1_ledbus0[31:16]), .col2(computer_1_ledbus1[15:0]),
    .col3(computer_1_ledbus1[31:16]), .col4(computer_1_ledbus2), .col5(computer_1_ledbus2_2),
    .col6(computer_1_ledbus3), .col7(computer_1_ledbus3_2), .col8(computer_1_ledbus4),
    .col9(computer_1_ledbus4_2), .col10(computer_1_ledbus5), .col11(computer_1_ledbus5_2),
    .col12(computer_1_ledbus6), .col13(computer_1_ledbus6_2), .col14(computer_1_ledbus7[15:0]),
    .col15(computer_1_ledbus7[31:16]));
  TTY tty_1 (.data(computer_1_ttycharout), .clk(computer_1_ttyclk), .we(computer_1_ttywritesig));  // open: clr
endmodule

module LEDMatrixInterface (
  input  Enable,
  input  CLK,
  input  Write,
  input  [31:0] Data,
  input  [25:0] Address,
  output [31:0] LB0,
  output [31:0] LB1,
  output [31:0] LB2,
  output [31:0] LB3,
  output [31:0] LB4,
  output [31:0] LB5,
  output [31:0] LB6,
  output [31:0] LB7,
  output [31:0] outputReadbuffer
);

  wire and_1_out, and_2_out, and_3_out, and_4_out, and_5_out, and_6_out, and_7_out, and_8_out, and_9_out,
       and_10_out, and_11_out, and_12_out, bitselector_1_out, bitselector_3_out, d_ff_1_q, decoder_1_out0,
       decoder_1_out1, decoder_1_out2, decoder_1_out3, decoder_1_out4, decoder_1_out5, decoder_1_out6,
       decoder_1_out7, not_1_out, not_2_out, not_3_out, not_4_out;
  wire [2:0] bitselector_2_out;
  wire [31:0] register_1_q, register_2_q, register_3_q, register_4_q, register_5_q, register_6_q,
       register_7_q, register_8_q;

  BitSelector #(.width(26)) bitselector_1 (.in(Address), .out(bitselector_1_out), .sel(5'b00011));
  BitSelector #(.width(26), .group(3)) bitselector_2 (.in(Address), .out(bitselector_2_out), .sel(4'b0000));
  BitSelector #(.width(26)) bitselector_3 (.in(Address), .out(bitselector_3_out), .sel(5'b00100));
  Decoder #(.select(3), .enable("false")) decoder_1 (
    .out0(decoder_1_out0), .out1(decoder_1_out1), .out2(decoder_1_out2), .out3(decoder_1_out3),
    .out4(decoder_1_out4), .out5(decoder_1_out5), .out6(decoder_1_out6), .out7(decoder_1_out7),
    .sel(bitselector_2_out));
  not not_1 (not_1_out, bitselector_3_out);
  not not_2 (not_2_out, bitselector_1_out);
  and and_1 (and_1_out, not_2_out, Write, not_1_out);
  not not_3 (not_3_out, bitselector_3_out);
  and and_2 (and_2_out, Write, not_3_out, bitselector_1_out);
  and and_3 (and_3_out, and_1_out, decoder_1_out0);
  and and_4 (and_4_out, and_1_out, decoder_1_out1);
  and and_5 (and_5_out, and_1_out, decoder_1_out2);
  and and_6 (and_6_out, and_1_out, decoder_1_out3);
  and and_7 (and_7_out, and_1_out, decoder_1_out4);
  and and_8 (and_8_out, and_1_out, decoder_1_out5);
  and and_9 (and_9_out, and_1_out, decoder_1_out6);
  and and_10 (and_10_out, and_1_out, decoder_1_out7);
  and and_11 (and_11_out, Enable, CLK);
  Register #(.width(32)) register_1 (.D(Data), .en(and_3_out), .Q(register_1_q), .clk(and_11_out));  // open: clr
  Register #(.width(32)) register_2 (.D(Data), .en(and_4_out), .Q(register_2_q), .clk(and_11_out));  // open: clr
  Register #(.width(32)) register_3 (.D(Data), .en(and_5_out), .Q(register_3_q), .clk(and_11_out));  // open: clr
  Register #(.width(32)) register_4 (.D(Data), .en(and_6_out), .Q(register_4_q), .clk(and_11_out));  // open: clr
  Register #(.width(32)) register_5 (.D(Data), .en(and_7_out), .Q(register_5_q), .clk(and_11_out));  // open: clr
  Register #(.width(32)) register_6 (.D(Data), .en(and_8_out), .Q(register_6_q), .clk(and_11_out));  // open: clr
  Register #(.width(32)) register_7 (.D(Data), .en(and_9_out), .Q(register_7_q), .clk(and_11_out));  // open: clr
  Register #(.width(32)) register_8 (.D(Data), .en(and_10_out), .Q(register_8_q), .clk(and_11_out));  // open: clr
  D_Flip_Flop d_ff_1 (.clk(and_11_out), .D(and_2_out), .Q(d_ff_1_q));  // open: Qn, preset, en, reset
  not not_4 (not_4_out, and_2_out);
  Register #(.width(32)) register_9 (.D(register_1_q), .en(d_ff_1_q), .Q(LB0), .clk(and_11_out), .clr(and_12_out));
  Register #(.width(32)) register_10 (.D(register_2_q), .en(d_ff_1_q), .Q(LB1), .clk(and_11_out), .clr(and_12_out));
  Register #(.width(32)) register_11 (.D(register_3_q), .en(d_ff_1_q), .Q(LB2), .clk(and_11_out), .clr(and_12_out));
  Register #(.width(32)) register_12 (.D(register_4_q), .en(d_ff_1_q), .Q(LB3), .clk(and_11_out), .clr(and_12_out));
  Register #(.width(32)) register_13 (.D(register_5_q), .en(d_ff_1_q), .Q(LB4), .clk(and_11_out), .clr(and_12_out));
  Register #(.width(32)) register_14 (.D(register_6_q), .en(d_ff_1_q), .Q(LB5), .clk(and_11_out), .clr(and_12_out));
  Register #(.width(32)) register_15 (.D(register_7_q), .en(d_ff_1_q), .Q(LB6), .clk(and_11_out), .clr(and_12_out));
  Register #(.width(32)) register_16 (.D(register_8_q), .en(d_ff_1_q), .Q(LB7), .clk(and_11_out), .clr(and_12_out));
  Multiplexer #(.select(3), .width(32), .enable("false")) multiplexer_1 (
    .in0(register_1_q), .in1(register_2_q), .in2(register_3_q), .in3(register_4_q), .in4(register_5_q),
    .in5(register_6_q), .in6(register_7_q), .in7(register_8_q), .out(outputReadbuffer),
    .sel(bitselector_2_out));
  and and_12 (and_12_out, not_4_out, Write, bitselector_3_out);

  // Notes on the sheet:
  //   256 bit frame buffer for LED Matrix
  //   Can write to 32 bit segments of the buffer
  //   When Address == 0x8 and write is Set the buffer will be loaded onto LED matrix
  //   When 5th bit is set the led matrix is cleared as long as 4th bit is not set
endmodule

module TTYInterface (
  input  enableDevice,
  input  write,
  input  [31:0] Data,
  input  CLK,
  output writeSigOut,
  output [6:0] charOut,
  output clkOut
);

  BitSelector #(.width(32), .group(7)) bitselector_1 (.in(Data), .out(charOut), .sel(3'b000));
  // Probe on charOut
  and and_1 (writeSigOut, enableDevice, write);

  assign clkOut = CLK;
endmodule

module KeyboardInterface (
  input  CLK,
  input  [6:0] keyboardChar,
  input  enableDevice,
  input  write,
  input  keyPress,
  input  [31:0] data,
  output ConsumeBuffer,
  output [31:0] \output ,
  output interruptSig
);

  wire and_1_out, bitselector_1_out, multiplexer_1_out;
  wire [1:1] and_2_out;
  wire [6:0] register_1_q;

  BitSelector #(.width(32)) bitselector_1 (.in(data), .out(bitselector_1_out), .sel({5{1'b0}}));
  and and_1 (and_1_out, CLK, enableDevice);
  and and_2 (and_2_out[1], write, bitselector_1_out);
  Multiplexer #(.select(2), .enable("false")) multiplexer_1 (
    .in0(interruptSig), .in1(1'b1), .in2(1'b0), .in3(1'b0), .out(multiplexer_1_out),
    .sel({and_2_out[1], keyPress}));
  D_Flip_Flop d_ff_1 (.clk(and_1_out), .D(multiplexer_1_out), .Q(interruptSig));  // open: Qn, preset, en, reset
  and and_3 (ConsumeBuffer, interruptSig, and_2_out[1]);
  Register #(.width(7)) register_1 (
    .D(keyboardChar), .en(multiplexer_1_out), .Q(register_1_q), .clk(and_1_out));  // open: clr
  assign \output  = {{25{1'b0}}, register_1_q};  // Bit_Extender bit_extender_1

  // Notes on the sheet:
  //   being written to output buffer.
  //   When keyboard device is enabled a new key press leads to an interrupt and the key pressed
  //   While device is in interrupt mode, until data is written to it with LSb set it remains in interrupt mode
endmodule
